// Logisim project Goncalves_Lucas_ULA.circ as structural Verilog: 2 circuits, main circuit main
module main (
  input  [3:0] A,
  input  [3:0] B,
  input  D,
  input  [2:0] in_4,
  output Overflow,
  output Zero,
  output [3:0] out_7
);

  ULA ula_1 (.A(A), .B(B), .in_4(in_4), .out_5(out_7), .Overflow(Overflow), .Zero(Zero), .D(D));
endmodule

module ULA (
  input  D,
  input  [3:0] A,
  input  [3:0] B,
  input  [2:0] in_4,
  output [3:0] out_5,
  output Overflow,
  output Zero
);

  wire and_1_out, and_2_out, decoder_1_out0, decoder_1_out1, decoder_1_out2, decoder_1_out3, decoder_1_out4,
       decoder_1_out5, decoder_1_out6, decoder_1_out7, not_1_out, subtractor_1_bout;
  wire [3:0] adder_1_out, controlled_buffer_6_out, or_2_out, shifter_1_out, shifter_2_out, subtractor_1_out;

  Decoder #(.select(3)) decoder_1 (
    .out0(decoder_1_out0), .out1(decoder_1_out1), .out2(decoder_1_out2), .out3(decoder_1_out3),
    .out4(decoder_1_out4), .out5(decoder_1_out5), .out6(decoder_1_out6), .out7(decoder_1_out7), .sel(in_4));  // open: en
  assign out_5 = decoder_1_out0 ? B : 4'bz;  // Controlled_Buffer controlled_buffer_1
  and and_1 (and_1_out, decoder_1_out7, decoder_1_out1);
  Adder #(.width(4)) adder_1 (.a(A), .b(B), .out(adder_1_out), .cout(decoder_1_out7));  // open: cin
  assign out_5 = decoder_1_out1 ? adder_1_out : 4'bz;  // Controlled_Buffer controlled_buffer_2
  and and_2 (and_2_out, subtractor_1_bout, decoder_1_out2);
  or or_1 (Overflow, and_1_out, and_2_out);
  Subtractor #(.width(4)) subtractor_1 (.a(A), .b(B), .out(subtractor_1_out), .bout(subtractor_1_bout));  // open: bin
  assign out_5 = decoder_1_out2 ? subtractor_1_out : 4'bz;  // Controlled_Buffer controlled_buffer_3
  assign or_2_out = B | A;  // OR_Gate or_2, 4 bits wide
  assign out_5 = decoder_1_out3 ? or_2_out : 4'bz;  // Controlled_Buffer controlled_buffer_4
  assign out_5 = decoder_1_out4 ? ~B : 4'bz;  // Controlled_Inverter controlled_inverter_1
  assign out_5 = decoder_1_out5 ? controlled_buffer_6_out : 4'bz;  // Controlled_Buffer controlled_buffer_5
  nor nor_1 (Zero, decoder_1_out7, decoder_1_out6, out_5[3], out_5[2], out_5[1], out_5[0]);
  Shifter #(.width(4)) shifter_1 (.in(A), .\dist (B[1:0]), .out(shifter_1_out));
  assign controlled_buffer_6_out = D ? shifter_2_out : 4'bz;  // Controlled_Buffer controlled_buffer_6
  Shifter #(.width(4), .shift("lr")) shifter_2 (.in(A), .\dist (B[1:0]), .out(shifter_2_out));
  not not_1 (not_1_out, D);
  assign controlled_buffer_6_out = not_1_out ? shifter_1_out : 4'bz;  // Controlled_Buffer controlled_buffer_7
endmodule
